// Logisim project ALU.circ as structural Verilog: 11 circuits, main circuit main
module main (
  input  [2:0] S,
  input  [15:0] A,
  input  [15:0] B,
  input  Enable,
  output [15:0] R,
  output Overflow,
  output Division_by_zero
);

  wire selection_1_division_by_zero, selection_1_overflow;
  wire [15:0] selection_1_r;

  Selection selection_1 (
    .A(A), .B(B), .S(S), .R(selection_1_r), .Overflow(selection_1_overflow),
    .Division_by_zero(selection_1_division_by_zero));
  Multiplexer #(.width(16)) multiplexer_1 (.in0({16{1'b0}}), .in1(selection_1_r), .out(R), .sel(Enable));  // open: en
  Multiplexer multiplexer_2 (.in0(1'b0), .in1(selection_1_overflow), .out(Overflow), .sel(Enable));  // open: en
  Multiplexer multiplexer_3 (
    .in0(1'b0), .in1(selection_1_division_by_zero), .out(Division_by_zero), .sel(Enable));  // open: en
endmodule

// ALU
module Selection (
  input  [2:0] S,
  input  [15:0] A,
  input  [15:0] B,
  output [15:0] R,
  output Overflow,
  output Division_by_zero
);

  wire n16bit_adder_1_overflow, n16bit_divider_1_overflow, n16bit_multiplier_1_overflow,
       n16bit_subtractor_1_overflow, nor_1_out;
  wire [15:0] n16bit_adder_1_out_3, n16bit_divider_1_out_3, n16bit_modulo_1_out_3, n16bit_multiplier_1_out_3,
       n16bit_subtractor_1_out_3;

  _16bit_Adder u_16bit_adder_1 (
    .in_1(A), .in_2(B), .out_3(n16bit_adder_1_out_3), .Overflow(n16bit_adder_1_overflow));  // open: Carry_Out
  _16bit_Subtractor u_16bit_subtractor_1 (
    .in_1(A), .in_2(B), .out_3(n16bit_subtractor_1_out_3), .Overflow(n16bit_subtractor_1_overflow));
  _16bit_Multiplier u_16bit_multiplier_1 (
    .in_1(A), .in_2(B), .out_3(n16bit_multiplier_1_out_3), .Overflow(n16bit_multiplier_1_overflow));
  _16bit_Divider u_16bit_divider_1 (
    .in_1(A), .in_2(B), .out_3(n16bit_divider_1_out_3), .Overflow(n16bit_divider_1_overflow));
  _16bit_Modulo u_16bit_modulo_1 (.in_1(A), .in_2(B), .out_3(n16bit_modulo_1_out_3));
  Multiplexer #(.select(3), .width(16), .enable("false")) multiplexer_1 (
    .in0(n16bit_adder_1_out_3), .in1(n16bit_subtractor_1_out_3), .in2(n16bit_multiplier_1_out_3),
    .in3(n16bit_divider_1_out_3), .in4(n16bit_modulo_1_out_3), .out(R), .sel(S));  // open: in5, in6, in7
  Multiplexer #(.select(3), .enable("false")) multiplexer_2 (
    .in0(n16bit_adder_1_overflow), .in1(n16bit_subtractor_1_overflow), .in2(n16bit_multiplier_1_overflow),
    .in3(n16bit_divider_1_overflow), .in4(1'b0), .out(Overflow), .sel(S));  // open: in5, in6, in7
  nor nor_1 (nor_1_out, B[0], B[1], B[2], B[3], B[4], B[5], B[6], B[7], B[8], B[9], B[10], B[11], B[12], B[13], B[14], B[15]);
  Multiplexer #(.select(3), .enable("false")) multiplexer_3 (
    .in0(1'b0), .in1(1'b0), .in2(1'b0), .in3(nor_1_out), .in4(nor_1_out), .out(Division_by_zero), .sel(S));  // open: in5, in6, in7
endmodule

// Add
module _16bit_Adder (
  input  [15:0] in_1,
  input  [15:0] in_2,
  output [15:0] out_3,
  output Carry_Out,
  output Overflow
);

  wire and_1_out, and_2_out, not_1_out, not_2_out, not_3_out;

  Adder #(.width(16)) adder_1 (.a(in_1), .b(in_2), .out(out_3), .cin(1'b0), .cout(Carry_Out));
  and and_1 (and_1_out, out_3[15], not_1_out, not_2_out);
  not not_1 (not_1_out, in_1[15]);
  not not_2 (not_2_out, in_2[15]);
  not not_3 (not_3_out, out_3[15]);
  and and_2 (and_2_out, not_3_out, in_1[15], in_2[15]);
  or or_1 (Overflow, and_1_out, and_2_out);
endmodule

// Inv
module Additive_Inverse (
  input  [15:0] in_1,
  output [15:0] out_2,
  output Overflow
);

  wire [15:0] not_1_out;

  assign not_1_out = ~in_1;  // NOT_Gate not_1, 16 bits wide
  _16bit_Adder u_16bit_adder_1 (.in_1(not_1_out), .in_2(16'h1), .out_3(out_2), .Overflow(Overflow));  // open: Carry_Out
endmodule

// Sub
module _16bit_Subtractor (
  input  [15:0] in_1,
  input  [15:0] in_2,
  output [15:0] out_3,
  output Overflow
);

  wire additive_inverse_1_overflow, n16bit_adder_1_overflow;
  wire [15:0] additive_inverse_1_out_2;

  Additive_Inverse additive_inverse_1 (
    .in_1(in_2), .out_2(additive_inverse_1_out_2), .Overflow(additive_inverse_1_overflow));
  _16bit_Adder u_16bit_adder_1 (
    .in_1(in_1), .in_2(additive_inverse_1_out_2), .out_3(out_3), .Overflow(n16bit_adder_1_overflow));  // open: Carry_Out
  xor xor_1 (Overflow, n16bit_adder_1_overflow, additive_inverse_1_overflow);
endmodule

// Abs
module Absolute_Value (
  input  [15:0] in_1,
  output [15:0] out_2,
  output Is_it_negative
);

  wire not_1_out;
  wire [15:0] additive_inverse_1_out_2;

  Additive_Inverse additive_inverse_1 (.in_1(in_1), .out_2(additive_inverse_1_out_2));  // open: Overflow
  not not_1 (not_1_out, in_1[15]);
  Multiplexer #(.width(16), .enable("false")) multiplexer_1 (
    .in0(additive_inverse_1_out_2), .in1(in_1), .out(out_2), .sel(not_1_out));

  assign Is_it_negative = in_1[15];
endmodule

// Mulx1
module _16x1_Multiplier (
  input  in_1,
  input  [15:0] in_2,
  output [15:0] out_3
);

  Multiplexer #(.width(16), .enable("false")) multiplexer_1 (.in0({16{1'b0}}), .in1(in_2), .out(out_3), .sel(in_1));
endmodule

// Shift
module _15bit_Shifter (
  input  [15:0] in_1,
  input  [4:0] in_2,
  output [15:0] out_3,
  output Overflow
);

  wire [31:16] shifter_1_out;

  Shifter #(.width(32)) shifter_1 (.in({{16{1'b0}}, in_1}), .\dist (in_2), .out({shifter_1_out, out_3}));
  or or_1 (Overflow, out_3[15], shifter_1_out[16], shifter_1_out[17], shifter_1_out[18], shifter_1_out[19], shifter_1_out[20], shifter_1_out[21], shifter_1_out[22], shifter_1_out[23], shifter_1_out[24], shifter_1_out[25], shifter_1_out[26], shifter_1_out[27], shifter_1_out[28], shifter_1_out[29], shifter_1_out[30], shifter_1_out[31]);
endmodule

// Mult
module _16bit_Multiplier (
  input  [15:0] in_1,
  input  [15:0] in_2,
  output [15:0] out_3,
  output Overflow
);

  wire absolute_value_1_is_it_negative, absolute_value_2_is_it_negative, additive_inverse_1_overflow,
       and_1_out, n15bit_shifter_1_overflow, n15bit_shifter_2_overflow, n15bit_shifter_3_overflow,
       n15bit_shifter_4_overflow, n15bit_shifter_5_overflow, n15bit_shifter_6_overflow,
       n15bit_shifter_7_overflow, n15bit_shifter_8_overflow, n15bit_shifter_9_overflow,
       n15bit_shifter_10_overflow, n15bit_shifter_11_overflow, n15bit_shifter_12_overflow,
       n15bit_shifter_13_overflow, n15bit_shifter_14_overflow, n15bit_shifter_15_overflow, not_1_out,
       or_1_out, xor_1_out;
  wire [15:0] absolute_value_1_out_2, absolute_value_2_out_2, adder_1_out, adder_2_out, adder_3_out,
       adder_4_out, adder_5_out, adder_6_out, adder_7_out, adder_8_out, adder_9_out, adder_10_out,
       adder_11_out, adder_12_out, adder_13_out, adder_14_out, adder_15_out, additive_inverse_1_out_2,
       n15bit_shifter_1_out_3, n15bit_shifter_2_out_3, n15bit_shifter_3_out_3, n15bit_shifter_4_out_3,
       n15bit_shifter_5_out_3, n15bit_shifter_6_out_3, n15bit_shifter_7_out_3, n15bit_shifter_8_out_3,
       n15bit_shifter_9_out_3, n15bit_shifter_10_out_3, n15bit_shifter_11_out_3, n15bit_shifter_12_out_3,
       n15bit_shifter_13_out_3, n15bit_shifter_14_out_3, n15bit_shifter_15_out_3, n16x1_multiplier_1_out_3,
       n16x1_multiplier_2_out_3, n16x1_multiplier_3_out_3, n16x1_multiplier_4_out_3,
       n16x1_multiplier_5_out_3, n16x1_multiplier_6_out_3, n16x1_multiplier_7_out_3,
       n16x1_multiplier_8_out_3, n16x1_multiplier_9_out_3, n16x1_multiplier_10_out_3,
       n16x1_multiplier_11_out_3, n16x1_multiplier_12_out_3, n16x1_multiplier_13_out_3,
       n16x1_multiplier_14_out_3, n16x1_multiplier_15_out_3, n16x1_multiplier_16_out_3;

  Absolute_Value absolute_value_1 (
    .in_1(in_2), .out_2(absolute_value_1_out_2), .Is_it_negative(absolute_value_1_is_it_negative));
  Absolute_Value absolute_value_2 (
    .in_1(in_1), .out_2(absolute_value_2_out_2), .Is_it_negative(absolute_value_2_is_it_negative));
  _16x1_Multiplier u_16x1_multiplier_1 (
    .in_1(absolute_value_1_out_2[0]), .in_2(absolute_value_2_out_2), .out_3(n16x1_multiplier_1_out_3));
  _16x1_Multiplier u_16x1_multiplier_2 (
    .in_1(absolute_value_1_out_2[1]), .in_2(absolute_value_2_out_2), .out_3(n16x1_multiplier_2_out_3));
  _16x1_Multiplier u_16x1_multiplier_3 (
    .in_1(absolute_value_1_out_2[2]), .in_2(absolute_value_2_out_2), .out_3(n16x1_multiplier_3_out_3));
  _16x1_Multiplier u_16x1_multiplier_4 (
    .in_1(absolute_value_1_out_2[3]), .in_2(absolute_value_2_out_2), .out_3(n16x1_multiplier_4_out_3));
  _16x1_Multiplier u_16x1_multiplier_5 (
    .in_1(absolute_value_1_out_2[4]), .in_2(absolute_value_2_out_2), .out_3(n16x1_multiplier_5_out_3));
  _16x1_Multiplier u_16x1_multiplier_6 (
    .in_1(absolute_value_1_out_2[5]), .in_2(absolute_value_2_out_2), .out_3(n16x1_multiplier_6_out_3));
  _16x1_Multiplier u_16x1_multiplier_7 (
    .in_1(absolute_value_1_out_2[6]), .in_2(absolute_value_2_out_2), .out_3(n16x1_multiplier_7_out_3));
  _16x1_Multiplier u_16x1_multiplier_8 (
    .in_1(absolute_value_1_out_2[7]), .in_2(absolute_value_2_out_2), .out_3(n16x1_multiplier_8_out_3));
  _16x1_Multiplier u_16x1_multiplier_9 (
    .in_1(absolute_value_1_out_2[8]), .in_2(absolute_value_2_out_2), .out_3(n16x1_multiplier_9_out_3));
  _16x1_Multiplier u_16x1_multiplier_10 (
    .in_1(absolute_value_1_out_2[9]), .in_2(absolute_value_2_out_2), .out_3(n16x1_multiplier_10_out_3));
  _16x1_Multiplier u_16x1_multiplier_11 (
    .in_1(absolute_value_1_out_2[10]), .in_2(absolute_value_2_out_2), .out_3(n16x1_multiplier_11_out_3));
  _16x1_Multiplier u_16x1_multiplier_12 (
    .in_1(absolute_value_1_out_2[11]), .in_2(absolute_value_2_out_2), .out_3(n16x1_multiplier_12_out_3));
  _16x1_Multiplier u_16x1_multiplier_13 (
    .in_1(absolute_value_1_out_2[12]), .in_2(absolute_value_2_out_2), .out_3(n16x1_multiplier_13_out_3));
  _16x1_Multiplier u_16x1_multiplier_14 (
    .in_1(absolute_value_1_out_2[13]), .in_2(absolute_value_2_out_2), .out_3(n16x1_multiplier_14_out_3));
  _16x1_Multiplier u_16x1_multiplier_15 (
    .in_1(absolute_value_1_out_2[14]), .in_2(absolute_value_2_out_2), .out_3(n16x1_multiplier_15_out_3));
  _16x1_Multiplier u_16x1_multiplier_16 (
    .in_1(absolute_value_1_out_2[15]), .in_2(absolute_value_2_out_2), .out_3(n16x1_multiplier_16_out_3));
  _15bit_Shifter u_15bit_shifter_1 (
    .in_1(n16x1_multiplier_2_out_3), .in_2(5'b00001), .out_3(n15bit_shifter_1_out_3),
    .Overflow(n15bit_shifter_1_overflow));
  _15bit_Shifter u_15bit_shifter_2 (
    .in_1(n16x1_multiplier_3_out_3), .in_2(5'b00010), .out_3(n15bit_shifter_2_out_3),
    .Overflow(n15bit_shifter_2_overflow));
  _15bit_Shifter u_15bit_shifter_3 (
    .in_1(n16x1_multiplier_4_out_3), .in_2(5'b00011), .out_3(n15bit_shifter_3_out_3),
    .Overflow(n15bit_shifter_3_overflow));
  _15bit_Shifter u_15bit_shifter_4 (
    .in_1(n16x1_multiplier_5_out_3), .in_2(5'b00100), .out_3(n15bit_shifter_4_out_3),
    .Overflow(n15bit_shifter_4_overflow));
  _15bit_Shifter u_15bit_shifter_5 (
    .in_1(n16x1_multiplier_6_out_3), .in_2(5'b00101), .out_3(n15bit_shifter_5_out_3),
    .Overflow(n15bit_shifter_5_overflow));
  _15bit_Shifter u_15bit_shifter_6 (
    .in_1(n16x1_multiplier_7_out_3), .in_2(5'b00110), .out_3(n15bit_shifter_6_out_3),
    .Overflow(n15bit_shifter_6_overflow));
  _15bit_Shifter u_15bit_shifter_7 (
    .in_1(n16x1_multiplier_8_out_3), .in_2(5'b00111), .out_3(n15bit_shifter_7_out_3),
    .Overflow(n15bit_shifter_7_overflow));
  _15bit_Shifter u_15bit_shifter_8 (
    .in_1(n16x1_multiplier_9_out_3), .in_2(5'b01000), .out_3(n15bit_shifter_8_out_3),
    .Overflow(n15bit_shifter_8_overflow));
  _15bit_Shifter u_15bit_shifter_9 (
    .in_1(n16x1_multiplier_10_out_3), .in_2(5'b01001), .out_3(n15bit_shifter_9_out_3),
    .Overflow(n15bit_shifter_9_overflow));
  _15bit_Shifter u_15bit_shifter_10 (
    .in_1(n16x1_multiplier_11_out_3), .in_2(5'b01010), .out_3(n15bit_shifter_10_out_3),
    .Overflow(n15bit_shifter_10_overflow));
  _15bit_Shifter u_15bit_shifter_11 (
    .in_1(n16x1_multiplier_12_out_3), .in_2(5'b01011), .out_3(n15bit_shifter_11_out_3),
    .Overflow(n15bit_shifter_11_overflow));
  _15bit_Shifter u_15bit_shifter_12 (
    .in_1(n16x1_multiplier_13_out_3), .in_2(5'b01100), .out_3(n15bit_shifter_12_out_3),
    .Overflow(n15bit_shifter_12_overflow));
  _15bit_Shifter u_15bit_shifter_13 (
    .in_1(n16x1_multiplier_14_out_3), .in_2(5'b01101), .out_3(n15bit_shifter_13_out_3),
    .Overflow(n15bit_shifter_13_overflow));
  _15bit_Shifter u_15bit_shifter_14 (
    .in_1(n16x1_multiplier_15_out_3), .in_2(5'b01110), .out_3(n15bit_shifter_14_out_3),
    .Overflow(n15bit_shifter_14_overflow));
  _15bit_Shifter u_15bit_shifter_15 (
    .in_1(n16x1_multiplier_16_out_3), .in_2(5'b01111), .out_3(n15bit_shifter_15_out_3),
    .Overflow(n15bit_shifter_15_overflow));
  xor xor_1 (xor_1_out, absolute_value_2_is_it_negative, absolute_value_1_is_it_negative);
  Adder #(.width(16)) adder_1 (
    .a(n16x1_multiplier_1_out_3), .b(n15bit_shifter_1_out_3), .out(adder_1_out), .cin(1'b0));  // open: cout
  Adder #(.width(16)) adder_2 (
    .a(adder_1_out), .b(n15bit_shifter_2_out_3), .out(adder_2_out), .cin(1'b0));  // open: cout
  Adder #(.width(16)) adder_3 (
    .a(adder_2_out), .b(n15bit_shifter_3_out_3), .out(adder_3_out), .cin(1'b0));  // open: cout
  Adder #(.width(16)) adder_4 (
    .a(adder_3_out), .b(n15bit_shifter_4_out_3), .out(adder_4_out), .cin(1'b0));  // open: cout
  Adder #(.width(16)) adder_5 (
    .a(adder_4_out), .b(n15bit_shifter_5_out_3), .out(adder_5_out), .cin(1'b0));  // open: cout
  Adder #(.width(16)) adder_6 (
    .a(adder_5_out), .b(n15bit_shifter_6_out_3), .out(adder_6_out), .cin(1'b0));  // open: cout
  Adder #(.width(16)) adder_7 (
    .a(adder_6_out), .b(n15bit_shifter_7_out_3), .out(adder_7_out), .cin(1'b0));  // open: cout
  Adder #(.width(16)) adder_8 (
    .a(adder_7_out), .b(n15bit_shifter_8_out_3), .out(adder_8_out), .cin(1'b0));  // open: cout
  Adder #(.width(16)) adder_9 (
    .a(adder_8_out), .b(n15bit_shifter_9_out_3), .out(adder_9_out), .cin(1'b0));  // open: cout
  Adder #(.width(16)) adder_10 (
    .a(adder_9_out), .b(n15bit_shifter_10_out_3), .out(adder_10_out), .cin(1'b0));  // open: cout
  Adder #(.width(16)) adder_11 (
    .a(adder_10_out), .b(n15bit_shifter_11_out_3), .out(adder_11_out), .cin(1'b0));  // open: cout
  Adder #(.width(16)) adder_12 (
    .a(adder_11_out), .b(n15bit_shifter_12_out_3), .out(adder_12_out), .cin(1'b0));  // open: cout
  Adder #(.width(16)) adder_13 (
    .a(adder_12_out), .b(n15bit_shifter_13_out_3), .out(adder_13_out), .cin(1'b0));  // open: cout
  Adder #(.width(16)) adder_14 (
    .a(adder_13_out), .b(n15bit_shifter_14_out_3), .out(adder_14_out), .cin(1'b0));  // open: cout
  Adder #(.width(16)) adder_15 (
    .a(adder_14_out), .b(n15bit_shifter_15_out_3), .out(adder_15_out), .cin(1'b0));  // open: cout
  Additive_Inverse additive_inverse_1 (
    .in_1(adder_15_out), .out_2(additive_inverse_1_out_2), .Overflow(additive_inverse_1_overflow));
  or or_1 (or_1_out, n15bit_shifter_1_overflow, n15bit_shifter_2_overflow, n15bit_shifter_3_overflow, n15bit_shifter_4_overflow, n15bit_shifter_5_overflow, n15bit_shifter_6_overflow, n15bit_shifter_7_overflow, n15bit_shifter_8_overflow, n15bit_shifter_9_overflow, n15bit_shifter_10_overflow, n15bit_shifter_11_overflow, n15bit_shifter_12_overflow, n15bit_shifter_13_overflow, n15bit_shifter_14_overflow, n15bit_shifter_15_overflow);
  Multiplexer #(.width(16), .enable("false")) multiplexer_1 (
    .in0(adder_15_out), .in1(additive_inverse_1_out_2), .out(out_3), .sel(xor_1_out));
  and and_1 (and_1_out, additive_inverse_1_overflow, not_1_out);
  not not_1 (not_1_out, xor_1_out);
  or or_2 (Overflow, and_1_out, or_1_out);
endmodule

// Div
module _16bit_Divider (
  input  [15:0] in_1,
  input  [15:0] in_2,
  output [15:0] out_3,
  output Overflow
);

  wire absolute_value_1_is_it_negative, absolute_value_2_is_it_negative, additive_inverse_1_overflow,
       not_1_out, xor_1_out;
  wire [15:0] absolute_value_1_out_2, absolute_value_2_out_2, additive_inverse_1_out_2, divider_1_out;

  Absolute_Value absolute_value_1 (
    .in_1(in_1), .out_2(absolute_value_1_out_2), .Is_it_negative(absolute_value_1_is_it_negative));
  Absolute_Value absolute_value_2 (
    .in_1(in_2), .out_2(absolute_value_2_out_2), .Is_it_negative(absolute_value_2_is_it_negative));
  Divider #(.width(16)) divider_1 (
    .a(absolute_value_1_out_2), .b(absolute_value_2_out_2), .out(divider_1_out));  // open: upper, rem
  xor xor_1 (xor_1_out, absolute_value_1_is_it_negative, absolute_value_2_is_it_negative);
  Additive_Inverse additive_inverse_1 (
    .in_1(divider_1_out), .out_2(additive_inverse_1_out_2), .Overflow(additive_inverse_1_overflow));
  Multiplexer #(.width(16), .enable("false")) multiplexer_1 (
    .in0(divider_1_out), .in1(additive_inverse_1_out_2), .out(out_3), .sel(xor_1_out));
  not not_1 (not_1_out, xor_1_out);
  and and_1 (Overflow, additive_inverse_1_overflow, not_1_out);
endmodule

// Mod
module _16bit_Modulo (
  input  [15:0] in_1,
  input  [15:0] in_2,
  output [15:0] out_3
);

  wire absolute_value_1_is_it_negative;
  wire [15:0] absolute_value_1_out_2, absolute_value_2_out_2, additive_inverse_1_out_2, divider_1_rem;

  Absolute_Value absolute_value_1 (
    .in_1(in_1), .out_2(absolute_value_1_out_2), .Is_it_negative(absolute_value_1_is_it_negative));
  Absolute_Value absolute_value_2 (.in_1(in_2), .out_2(absolute_value_2_out_2));  // open: Is_it_negative
  Divider #(.width(16)) divider_1 (
    .a(absolute_value_1_out_2), .b(absolute_value_2_out_2), .rem(divider_1_rem));  // open: out, upper
  Additive_Inverse additive_inverse_1 (.in_1(divider_1_rem), .out_2(additive_inverse_1_out_2));  // open: Overflow
  Multiplexer #(.width(16), .enable("false")) multiplexer_1 (
    .in0(divider_1_rem), .in1(additive_inverse_1_out_2), .out(out_3), .sel(absolute_value_1_is_it_negative));
endmodule
