// Logisim project Main.circ as structural Verilog: 5 circuits, main circuit main
module main (
  output [7:0] out_1,
  output [15:0] out_2,
  output [15:0] out_3,
  output [5:0] out_4
);

  wire and_1_out, and_2_out, clock_1_out, clock_2_out, clock_3_out, clock_4_out, \end , load_ram, not_1_out,
       or_1_out, phase_0, phase_1, select_pc, store_acc, store_ram;
  wire [7:0] Control_address, multiplexer_1_out;
  wire [15:0] ACC_q;

  Program_Counter PC (.Address(Control_address), .select(select_pc), .overwrite(phase_1), .out_4(out_1));
  Multiplexer #(.width(8), .enable("false")) multiplexer_1 (
    .in0(out_1), .in1(Control_address), .out(multiplexer_1_out), .sel(phase_1));
  Flags flags_1 (.in_1(ACC_q), .GT(out_4));
  Control Control (
    .in_1(out_3), .address(Control_address), .store_acc(store_acc), .load_ram(load_ram),
    .store_ram(store_ram), .select_pc(select_pc), .\end (\end ));
  Register_part #(.width(16)) ACC (.D(out_2), .en(and_1_out), .Q(ACC_q), .clk(clock_1_out));  // open: clr
  and and_1 (and_1_out, store_acc, phase_1);
  Clock clock_1 (.out(clock_1_out));
  and and_2 (and_2_out, store_ram, phase_1);
  Counter #(.width(1), .max('h1)) counter_1 (.Q(phase_1), .clk(not_1_out));  // open: load, D, count, carry, clr
  not not_1 (not_1_out, clock_2_out);
  Clock clock_2 (.out(clock_2_out));
  or or_1 (or_1_out, load_ram, phase_0);
  Clock clock_3 (.out(clock_3_out));
  not not_2 (phase_0, phase_1);
  RAM #(.dataWidth(16), .bus("separate")) ram_1 (
    .addr(multiplexer_1_out), .din(ACC_q), .data(out_2), .str(and_2_out), .sel(\end ), .clk(clock_3_out),
    .ld(or_1_out));  // open: clr
  Register_part #(.width(16)) IR (.D(out_2), .en(phase_0), .Q(out_3), .clk(clock_4_out));  // open: clr
  Clock clock_4 (.out(clock_4_out));

  // Notes on the sheet:
  //   Marcador de Fase
endmodule

module Register (
  input  [7:0] in,
  input  load,
  output [7:0] out
);

  D_Flip_Flop d_ff_1 (.clk(load), .D(in[0]), .Q(out[0]));  // open: Qn, preset, en, reset
  D_Flip_Flop d_ff_2 (.clk(load), .D(in[1]), .Q(out[1]));  // open: Qn, preset, en, reset
  D_Flip_Flop d_ff_3 (.clk(load), .D(in[2]), .Q(out[2]));  // open: Qn, preset, en, reset
  D_Flip_Flop d_ff_4 (.clk(load), .D(in[3]), .Q(out[3]));  // open: Qn, preset, en, reset
  D_Flip_Flop d_ff_5 (.clk(load), .D(in[4]), .Q(out[4]));  // open: Qn, preset, en, reset
  D_Flip_Flop d_ff_6 (.clk(load), .D(in[5]), .Q(out[5]));  // open: Qn, preset, en, reset
  D_Flip_Flop d_ff_7 (.clk(load), .D(in[6]), .Q(out[6]));  // open: Qn, preset, en, reset
  D_Flip_Flop d_ff_8 (.clk(load), .D(in[7]), .Q(out[7]));  // open: Qn, preset, en, reset
endmodule

module Control (
  input  [15:0] in_1,
  output [7:0] address,
  output store_acc,
  output load_ram,
  output store_ram,
  output select_pc,
  output \end 
);

  wire and_3_out, not_1_out, not_2_out, not_3_out, not_5_out, not_6_out;

  not not_1 (not_1_out, in_1[10]);
  not not_2 (not_2_out, in_1[9]);
  not not_3 (not_3_out, in_1[8]);
  // NOT_Gate not_4 has open pins: in=in_1[10], out=open
  and and_1 (load_ram, in_1[8], in_1[9], not_1_out, in_1[11]);
  and and_2 (store_ram, not_2_out, in_1[10], in_1[11]);
  and and_3 (and_3_out, not_3_out, in_1[9]);
  not not_5 (not_5_out, in_1[12]);
  not not_6 (not_6_out, in_1[13]);
  or or_1 (select_pc, and_3_out, not_5_out, not_6_out);
  not not_7 (\end , in_1[14]);

  assign address = in_1[7:0];
  assign store_acc = load_ram;
endmodule

module Program_Counter (
  input  [7:0] Address,
  input  select,
  input  overwrite,
  output [7:0] out_4
);

  wire [7:0] multiplexer_1_out, n8bit_adder_1_out_3;

  Multiplexer #(.width(8), .enable("false")) multiplexer_1 (
    .in0(Address), .in1(n8bit_adder_1_out_3), .out(multiplexer_1_out), .sel(select));
  _8bit_Adder u_8bit_adder_1 (.in_1(8'h1), .in_2(out_4), .out_3(n8bit_adder_1_out_3));  // open: Carry_Out, Overflow
  Register register_1 (.in(multiplexer_1_out), .load(overwrite), .out(out_4));
endmodule

module Flags (
  input  [15:0] in_1,
  output [5:0] GT
);

  wire not_1_out, not_2_out;

  or or_1 (GT[1], in_1[0], in_1[1], in_1[2], in_1[3], in_1[4], in_1[5], in_1[6], in_1[7], in_1[8], in_1[9], in_1[10], in_1[11], in_1[12], in_1[13], in_1[14], in_1[15]);
  not not_1 (not_1_out, GT[1]);
  not not_2 (not_2_out, in_1[15]);
  not not_3 (GT[3], GT[1]);
  not not_4 (GT[5], in_1[15]);
  or or_2 (GT[0], not_1_out, in_1[15]);
  and and_1 (GT[2], not_2_out, GT[1]);

  assign GT[4] = in_1[15];

  // Notes on the sheet:
  //   LE
  //   DZ
  //   EQ
  //   GE
  //   LT
endmodule
